// Logisim project memoryGame.circ as structural Verilog
module main (
  output [3:0] out_1
);

  wire COLUNA, CONFIRMA, L00, L01, L02, L03, L10, L11, L12, L13, L20, L21, L22, L23, L30, L31, L32, L33,
       LINHA, P1, P2;
  wire [3:0] _00, _01, _02, _03, _10, _11, _12, _13, _20, _21, _22, _23, _30, _31, _32, _33, PONTOS_P1,
       PONTOS_P2;

  Button button_1 (.out(CONFIRMA));
  Button button_2 (.out(LINHA));
  Button button_3 (.out(COLUNA));
  LED led_1 (.in(P1));
  Hex_Digit_Display hex_digit_display_1 (.value(PONTOS_P1));  // open: dp
  LED led_2 (.in(P2));
  Hex_Digit_Display hex_digit_display_2 (.value(PONTOS_P2));  // open: dp
  LED led_3 (.in(L00));
  Hex_Digit_Display hex_digit_display_3 (.value(_00));  // open: dp
  LED led_4 (.in(L10));
  Hex_Digit_Display hex_digit_display_4 (.value(_10));  // open: dp
  LED led_5 (.in(L20));
  Hex_Digit_Display hex_digit_display_5 (.value(_20));  // open: dp
  LED led_6 (.in(L30));
  Hex_Digit_Display hex_digit_display_6 (.value(_30));  // open: dp
  LED led_7 (.in(L01));
  Hex_Digit_Display hex_digit_display_7 (.value(_01));  // open: dp
  LED led_8 (.in(L11));
  Hex_Digit_Display hex_digit_display_8 (.value(_11));  // open: dp
  LED led_9 (.in(L21));
  Hex_Digit_Display hex_digit_display_9 (.value(_21));  // open: dp
  LED led_10 (.in(L31));
  Hex_Digit_Display hex_digit_display_10 (.value(_31));  // open: dp
  LED led_11 (.in(L02));
  Hex_Digit_Display hex_digit_display_11 (.value(_02));  // open: dp
  LED led_12 (.in(L12));
  Hex_Digit_Display hex_digit_display_12 (.value(_12));  // open: dp
  LED led_13 (.in(L22));
  Hex_Digit_Display hex_digit_display_13 (.value(_22));  // open: dp
  LED led_14 (.in(L32));
  Hex_Digit_Display hex_digit_display_14 (.value(_32));  // open: dp
  LED led_15 (.in(L03));
  Hex_Digit_Display hex_digit_display_15 (.value(_03));  // open: dp
  LED led_16 (.in(L13));
  Hex_Digit_Display hex_digit_display_16 (.value(_13));  // open: dp
  LED led_17 (.in(L23));
  Hex_Digit_Display hex_digit_display_17 (.value(_23));  // open: dp
  LED led_18 (.in(L33));
  Hex_Digit_Display hex_digit_display_18 (.value(_33));  // open: dp
  Demultiplexer #(.select(4), .enable("false")) demultiplexer_1 (
    .out0(L00), .out1(L01), .out2(L02), .out3(L03), .out4(L10), .out5(L11), .out6(L12), .out7(L13),
    .out8(L20), .out9(L20), .out10(L20), .out11(L20), .out12(L20), .out13(L20), .out14(L20), .out15(L20),
    .in(1'b1), .sel(out_1));
  Counter #(.width(2), .max('h3)) counter_1 (.Q(out_1[1:0]), .clk(COLUNA));  // open: load, D, count, carry, clr
  Counter #(.width(2), .max('h3)) counter_2 (.Q(out_1[3:2]), .clk(LINHA));  // open: load, D, count, carry, clr

  // Other names for the same wires on the sheet: xy[3:0] = out_1

  // Notes on the sheet:
  //   JOGO DA MEMÓRIA
endmodule
